# Fritzing sketch Remote_sketch (saved by Fritzing 0.9.3b)
breadboards: 1

parts:
  Part2 = Arduino Nano (Rev3.0)
  S1 = Pushbutton [package="[THT]"]
  S2 = Pushbutton [package="[THT]"]
  S3 = Pushbutton [package="[THT]"]
  S4 = Pushbutton [package="[THT]"]
  S5 = Pushbutton [package="[THT]"]
  S6 = Pushbutton [package="[THT]"]
  R3 = Resistor [tolerance=±5% resistance=10k package=THT]
  R4 = Resistor [tolerance=±5% resistance=10k package=THT]
  R5 = Resistor [tolerance=±5% resistance=10k package=THT]
  R6 = Resistor [tolerance=±5% resistance=10k package=THT]
  R7 = Resistor [tolerance=±5% resistance=10k package=THT]
  R9 = Resistor [tolerance=±5% resistance=10k package=THT]
  LED1 = Infrared LED - 5mm [package="5 mm [THT]"]

nets:
  N1: Part2.GND, R3.Pin_0, R4.Pin_1, R5.Pin_0, R6.Pin_0, R7.Pin_0, R9.Pin_1, LED1.anode
  N2: Part2.D2, S3.Pin_3, S3.Pin_4, R4.Pin_0
  N3: Part2.D3, LED1.cathode
  N4: Part2.D4, S6.Pin_3, S6.Pin_4, R9.Pin_0
  N5: Part2.D5, S4.Pin_3, S4.Pin_4, R5.Pin_1
  N6: Part2.D6, S5.Pin_3, S5.Pin_4, R3.Pin_1
  N7: Part2.D7, S1.Pin_3, S1.Pin_4, R6.Pin_1
  N8: Part2.D8, S2.Pin_3, S2.Pin_4, R7.Pin_1
  N9: Part2.5V, S4.Pin_1, S4.Pin_2
  N10: S1.Pin_1, S1.Pin_2
  N11: S2.Pin_1, S2.Pin_2
  N12: S3.Pin_1, S3.Pin_2
  N13: S5.Pin_1, S5.Pin_2
  N14: S6.Pin_1, S6.Pin_2

notes:
  5V here

custom parts:
  Infrared LED - 5mm: A generic infrared LED (~1.2V)
